# Fritzing sketch Схема (saved by Fritzing 0.9.3b)
breadboards: 1

parts:
  U2 = NodeMCU V3.0
  R1 = Resistor [tolerance=±5% resistance=220 package=THT]
  R2 = Rotary Potentiometer (Small) [maximum_resistance=100kΩ package=THT]
  S1 = Pushbutton [package="[THT]"]
  LED1 = LED - 5mm [color="Red (633nm)" package="5 mm [THT]"]
  S2 = Pushbutton [package="[THT]"]
  S3 = Pushbutton [package="[THT]"]
  R3 = Resistor [tolerance=±5% resistance=220 package=THT]
  R4 = Resistor [tolerance=±5% resistance=220 package=THT]

nets:
  N1: U2.D4, R1.Pin_1
  N2: U2.3V3, R2.leg2, S1.Pin_3, S1.Pin_4, R3.Pin_0
  N3: U2.GND#6, U2.GND#13, U2.GND#16, U2.GND#33, R2.leg1, LED1.cathode, S2.Pin_3, S2.Pin_4, S3.Pin_3, S3.Pin_4, R4.Pin_0
  N4: U2.D5, S1.Pin_1, S1.Pin_2, R4.Pin_1
  N5: U2.D6, S2.Pin_1, S2.Pin_2
  N6: U2.D7, S3.Pin_1, S3.Pin_2, R3.Pin_1
  N7: U2.A0, R2.wiper
  N8: R1.Pin_0, LED1.anode

custom parts:
  NodeMCU V3.0: ESP8266 based NodeMCU
